# Fritzing sketch wdt (saved by Fritzing 0.9.3b)
breadboards: 1

parts:
  D1 = Rectifier Diode [part_number=1N4001 package="300 mil [THT]"]
  D2 = Rectifier Diode [part_number=1N4001 package="300 mil [THT]"]
  R3 = Resistor [tolerance=±5% resistance=330 package=THT]
  R1 = Resistor [tolerance=±5% resistance=1M package=THT]
  R5 = Resistor [tolerance=±5% resistance=330 package=THT]
  R4 = Resistor [tolerance=±5% resistance=330 package=THT]
  LED1 = LED - 5mm [color="Red (633nm)" package="5 mm [THT]"]
  LED2 = LED - 5mm [color="White (6500K)" package="5 mm [THT]"]
  Q1 = PNP-Transistor [part_number="PNP 2907A" package="TO92 [THT]"]
  C1 = Electrolytic Capacitor [capacitance=22µF package="100 mil [THT, electrolytic]"]
  R2 = Resistor [tolerance=±5% resistance=4.7k package=THT]
  C2 = Tantalum Capacitor [capacitance=0.1µF package="100 mil [THT, tantalum]"]
  パーツ1 = Arduino Uno (Rev3)
  IC1 = 555 Timer [package="SO8 [SMD]"]
  WeMos_D1_Mini1 = WeMos D1 Mini  # not connected
  WeMos_D1_Mini2 = WeMos D1 Mini  # not connected

nets:
  N1: D1.cathode, LED2.anode, IC1.Pin_3
  N2: D1.anode, パーツ1.RESET
  N3: D2.cathode, Q1.B, パーツ1.D10_PWM/SS
  N4: D2.anode, R4.Pin_1
  N5: R3.Pin_0, LED1.anode
  5V: R3.Pin_1, R1.Pin_1, パーツ1.5V, IC1.Pin_4, IC1.Pin_8
  N6: R1.Pin_0, R2.Pin_0, IC1.Pin_7
  GND: R5.Pin_0, Q1.C, C1.-, C2.-, パーツ1.GND, IC1.Pin_1
  N7: R5.Pin_1, LED2.cathode
  N8: R4.Pin_0, C1.+, R2.Pin_1, IC1.Pin_2, IC1.Pin_6
  N9: LED1.cathode, Q1.E
  N10: C2.+, IC1.Pin_5
