# Fritzing sketch wdtmini (saved by Fritzing 0.9.3b)
breadboards: 1

parts:
  D1 = Rectifier Diode [part_number=1N4001 package="300 mil [THT]"]
  R1 = Resistor [tolerance=±5% resistance=1M package=THT]
  R4 = Resistor [tolerance=±5% resistance=330 package=THT]
  C1 = Electrolytic Capacitor [capacitance=22µF package="100 mil [THT, electrolytic]"]
  R2 = Resistor [tolerance=±5% resistance=4.7k package=THT]
  C2 = Tantalum Capacitor [capacitance=0.1µF package="100 mil [THT, tantalum]"]
  パーツ1 = Arduino Uno (Rev3)
  IC1 = 555 Timer [package="SO8 [SMD]"]

nets:
  N1: D1.cathode, IC1.Pin_3
  N2: D1.anode, パーツ1.RESET
  N3: R1.Pin_0, R2.Pin_0, IC1.Pin_7
  5V: R1.Pin_1, パーツ1.5V, IC1.Pin_4, IC1.Pin_8
  N4: R4.Pin_0, C1.+, R2.Pin_1, IC1.Pin_2, IC1.Pin_6
  N5: R4.Pin_1, パーツ1.D10_PWM/SS
  GND: C1.-, C2.-, パーツ1.GND, IC1.Pin_1
  N6: C2.+, IC1.Pin_5
